// Logisim project mini_computer.circ as structural Verilog
module _8_bit_RAM (
  input  Adress,
  input  in_2,
  input  in_3,
  input  Write,
  input  Data_In,
  input  Clear,
  output out_7
);

  wire n3_8_decoder_1_d0, n3_8_decoder_1_d1, n3_8_decoder_1_d2, n3_8_decoder_1_d3, n3_8_decoder_1_d4,
       n3_8_decoder_1_d5, n3_8_decoder_1_d6, n3_8_decoder_1_d7, n8_bit_latch_1_out_11, n8_bit_latch_1_out_12,
       n8_bit_latch_1_out_13, n8_bit_latch_1_out_14, n8_bit_latch_1_out_15, n8_bit_latch_1_out_16,
       n8_bit_latch_1_out_17, n8_bit_latch_1_out_18;

  _8_bit_Latch u_8_bit_latch_1 (
    .Write(n3_8_decoder_1_d7), .Clear(Clear), .out_11(n8_bit_latch_1_out_11), .out_12(n8_bit_latch_1_out_12),
    .out_13(n8_bit_latch_1_out_13), .out_14(n8_bit_latch_1_out_14), .out_15(n8_bit_latch_1_out_15),
    .out_16(n8_bit_latch_1_out_16), .out_17(n8_bit_latch_1_out_17), .out_18(n8_bit_latch_1_out_18),
    .Data_In(Data_In), .in_2(n3_8_decoder_1_d6), .in_3(n3_8_decoder_1_d5), .in_4(n3_8_decoder_1_d4),
    .in_5(n3_8_decoder_1_d3), .in_6(n3_8_decoder_1_d2), .in_7(n3_8_decoder_1_d1), .in_8(n3_8_decoder_1_d0));
  _8_1_Selector u_8_1_selector_1 (
    .D0(n8_bit_latch_1_out_18), .D0_2(n8_bit_latch_1_out_17), .D0_3(n8_bit_latch_1_out_16),
    .D0_4(n8_bit_latch_1_out_15), .D0_5(n8_bit_latch_1_out_14), .D0_6(n8_bit_latch_1_out_13),
    .D0_7(n8_bit_latch_1_out_12), .D0_8(n8_bit_latch_1_out_11), .S0(Adress), .S1(in_2), .S2(in_3),
    .Data_Out(out_7));
  _3_8_Decoder u_3_8_decoder_1 (
    .Data_In(Write), .S0(Adress), .S1(in_2), .S2(in_3), .D0(n3_8_decoder_1_d0), .D1(n3_8_decoder_1_d1),
    .D2(n3_8_decoder_1_d2), .D3(n3_8_decoder_1_d3), .D4(n3_8_decoder_1_d4), .D5(n3_8_decoder_1_d5),
    .D6(n3_8_decoder_1_d6), .D7(n3_8_decoder_1_d7));
endmodule

module D_flip_flop (
  input  Clear,
  input  Clock,
  input  Data_In,
  output Data_Out,
  output Data_Out__Complement
);

  wire and_1_out, and_2_out, not_1_out, or_1_out;

  not not_1 (not_1_out, Data_In);
  and and_1 (and_1_out, not_1_out, Clock);
  and and_2 (and_2_out, Clock, Data_In);
  or or_1 (or_1_out, Clear, and_1_out);
  nor nor_1 (Data_Out, or_1_out, Data_Out__Complement);
  nor nor_2 (Data_Out__Complement, Data_Out, and_2_out);
endmodule

module D_flip_flop_edge (
  input  Clock,
  input  Data,
  output Data_Out,
  output Data_Out___Compliment
);

  wire _1, _2, and_1_out, and_2_out, and_3_out, and_4_out, not_1_out, not_2_out;

  and and_1 (and_1_out, Data, not_1_out);
  not not_1 (not_1_out, Clock);
  and and_2 (and_2_out, not_1_out, not_2_out);
  not not_2 (not_2_out, Data);
  nor nor_1 (_1, and_1_out, _2);
  nor nor_2 (_2, _1, and_2_out);
  and and_3 (and_3_out, _1, Clock);
  and and_4 (and_4_out, Clock, _2);
  nor nor_3 (Data_Out, Data_Out___Compliment, and_3_out);
  nor nor_4 (Data_Out___Compliment, and_4_out, Data_Out);

  // Other names for the same wires on the sheet: _3 = Data_Out___Compliment; _4 = Data_Out

  // Notes on the sheet:
  //   An edge triggered D-flip-flop.
endmodule

module _3_8_Decoder (
  input  Data_In,
  input  S0,
  input  S1,
  input  S2,
  output D0,
  output D1,
  output D2,
  output D3,
  output D4,
  output D5,
  output D6,
  output D7
);

  wire not_1_out, not_2_out, not_3_out;

  not not_1 (not_1_out, S0);
  not not_2 (not_2_out, S1);
  not not_3 (not_3_out, S2);
  and and_1 (D0, Data_In, S0, S1, S2);
  and and_2 (D1, Data_In, S0, S1, not_3_out);
  and and_3 (D2, Data_In, S0, not_2_out, S2);
  and and_4 (D3, Data_In, S0, not_2_out, not_3_out);
  and and_5 (D4, Data_In, not_1_out, S1, S2);
  and and_6 (D5, Data_In, not_1_out, S1, not_3_out);
  and and_7 (D6, Data_In, not_1_out, not_2_out, S2);
  and and_8 (D7, Data_In, not_1_out, not_2_out, not_3_out);

  // Notes on the sheet:
  //   Outputs data to one of eight different outputs based on a three bit switch
endmodule

module _8_1_Selector (
  input  D0,
  input  D0_2,
  input  D0_3,
  input  D0_4,
  input  D0_5,
  input  D0_6,
  input  D0_7,
  input  D0_8,
  input  S0,
  input  S1,
  input  S2,
  output Data_Out
);

  wire and_1_out, and_2_out, and_3_out, and_4_out, and_5_out, and_6_out, and_7_out, and_8_out, not_1_out,
       not_2_out, not_3_out;

  not not_1 (not_1_out, S0);
  not not_2 (not_2_out, S1);
  not not_3 (not_3_out, S2);
  and and_1 (and_1_out, S0, S1, S2, D0);
  and and_2 (and_2_out, S0, S1, not_3_out, D0_2);
  and and_3 (and_3_out, S0, not_2_out, S2, D0_3);
  and and_4 (and_4_out, S0, not_2_out, not_3_out, D0_4);
  and and_5 (and_5_out, not_1_out, S1, S2, D0_5);
  and and_6 (and_6_out, not_1_out, S1, not_3_out, D0_6);
  and and_7 (and_7_out, not_1_out, not_2_out, S2, D0_7);
  and and_8 (and_8_out, not_1_out, not_2_out, not_3_out, D0_8);
  or or_1 (Data_Out, and_1_out, and_2_out, and_3_out, and_4_out, and_5_out, and_6_out, and_7_out, and_8_out);
endmodule

module _8_bit_Latch (
  input  Write,
  input  in_2,
  input  in_3,
  input  in_4,
  input  in_5,
  input  in_6,
  input  in_7,
  input  in_8,
  input  Clear,
  input  Data_In,
  output out_11,
  output out_12,
  output out_13,
  output out_14,
  output out_15,
  output out_16,
  output out_17,
  output out_18
);

  D_Flip_Flop d_ff_1 (.clk(Write), .D(Data_In), .Q(out_11), .reset(Clear));  // open: Qn, preset, en
  D_Flip_Flop d_ff_2 (.clk(in_2), .D(Data_In), .Q(out_12), .reset(Clear));  // open: Qn, preset, en
  D_Flip_Flop d_ff_3 (.clk(in_3), .D(Data_In), .Q(out_13), .reset(Clear));  // open: Qn, preset, en
  D_Flip_Flop d_ff_4 (.clk(in_4), .D(Data_In), .Q(out_14), .reset(Clear));  // open: Qn, preset, en
  D_Flip_Flop d_ff_5 (.clk(in_5), .D(Data_In), .Q(out_15), .reset(Clear));  // open: Qn, preset, en
  D_Flip_Flop d_ff_6 (.clk(in_6), .D(Data_In), .Q(out_16), .reset(Clear));  // open: Qn, preset, en
  D_Flip_Flop d_ff_7 (.clk(in_7), .D(Data_In), .Q(out_17), .reset(Clear));  // open: Qn, preset, en
  D_Flip_Flop d_ff_8 (.clk(in_8), .D(Data_In), .Q(out_18), .reset(Clear));  // open: Qn, preset, en
endmodule

module counter (
  input  Reset,
  output out_2,
  output out_3,
  output out_4,
  output out_5
);

  wire clock_1_out, d_ff_1_qn, d_ff_2_qn, d_ff_3_qn, d_ff_4_qn;

  Clock clock_1 (.out(clock_1_out));
  D_Flip_Flop d_ff_1 (.clk(clock_1_out), .D(d_ff_1_qn), .Q(out_2), .Qn(d_ff_1_qn), .reset(Reset));  // open: preset, en
  D_Flip_Flop d_ff_2 (.clk(d_ff_1_qn), .D(d_ff_2_qn), .Q(out_3), .Qn(d_ff_2_qn), .reset(Reset));  // open: preset, en
  D_Flip_Flop d_ff_3 (.clk(d_ff_2_qn), .D(d_ff_3_qn), .Q(out_4), .Qn(d_ff_3_qn), .reset(Reset));  // open: preset, en
  D_Flip_Flop d_ff_4 (.clk(d_ff_3_qn), .D(d_ff_4_qn), .Q(out_5), .Qn(d_ff_4_qn), .reset(Reset));  // open: preset, en
endmodule
